# Fritzing sketch parnik (saved by Fritzing 0.9.0b)
breadboards: 2

parts:
  Часть1 = Arduino Uno (Rev3)
  LCD1 = LCD screen
  J1 = Screw terminal - 2 pins [package=THT]
  R1 = Trimmer Potentiometer [maximum_resistance=10kΩ package=THT]  # not connected
  R2 = Trimmer Potentiometer [maximum_resistance=10kΩ package=THT]  # not connected
  R3 = Resistor [tolerance=±5% resistance=220 package=THT]
  J2 = Screw terminal - 2 pins [package=THT]
  J3 = Screw terminal - 2 pins [package=THT]
  R4 = Resistor [tolerance=±5% resistance=220 package=THT]
  R5 = Resistor [tolerance=±5% resistance=220 package=THT]
  Q1 = Basic FET P-Channel [package="TO220 [THT]"]
  J4 = Screw terminal - 2 pins [package=THT]
  U1 = 74HC4052 [package=dil16]
  J5 = Screw terminal - 2 pins [package=THT]
  K1 = Relay [part_number=FRS1B-S package=THT]

nets:
  N1: Часть1.A5/SCL, R4.Pin_1, R5.Pin_0
  N2: Часть1.D8, LCD1.DB6
  N3: Часть1.D9_PWM, LCD1.DB7
  N4: Часть1.D10_PWM/SS, J1.pin2, R3.Pin_1
  N5: Часть1.D11_PWM/MOSI, U1.Y0
  N6: Часть1.D12/MISO, Q1.gate
  N7: Часть1.D3_PWM, LCD1.RS
  N8: Часть1.D5_PWM, LCD1.E
  N9: Часть1.D6_PWM, LCD1.DB4
  N10: Часть1.D7, LCD1.DB5
  5V: Часть1.5V, LCD1.VDD, LCD1.LED+, R3.Pin_0
  GND: Часть1.GND, LCD1.VSS, LCD1.V0, LCD1.R/W, LCD1.LED-, J2.pin2, J3.pin2, R4.Pin_0, Q1.source, U1.GND, J5.pin2
  N11: J2.pin1, J3.pin1, R5.Pin_1, J4.pin2, U1.B, K1.C1, K1.C2, K1.B
  N12: Q1.drain, J4.pin1
  N13: U1.VCC, K1.A
  N14: J5.pin1, K1.COIL1
